# Fritzing sketch SPLUNK IOT Prototype (saved by Fritzing 0.9.3b)
circuit board: 7.42114cm x 2.54573cm
breadboards: 1

parts:
  R6 = Resistor [tolerance=±5% resistance=680 package=THT]
  R9 = Resistor [tolerance=±5% resistance=100 package=THT]
  R2 = Resistor [tolerance=±5% resistance=470 package=THT]
  R8 = Resistor [tolerance=±5% resistance=2.2k package=THT]
  R5 = Resistor [tolerance=±5% resistance=1.1k package=THT]
  R1 = Resistor [tolerance=±5% resistance=3.3k package=THT]
  R7 = Resistor [tolerance=±5% resistance=3.3k package=THT]
  D1 = Rectifier Diode [part_number=1N4001 package="300 mil [THT]"]
  D2 = Rectifier Diode [part_number=1N4001 package="300 mil [THT]"]
  R10 = Resistor [tolerance=±5% resistance=1k package=THT]
  R3 = Resistor [tolerance=±5% resistance=1.1k package=THT]
  R4 = Resistor [tolerance=±5% resistance=680 package=THT]
  R12 = Resistor [tolerance=±5% resistance=220 package=THT]
  R11 = Resistor [tolerance=±5% resistance=2.2k package=THT]
  R13 = Resistor [tolerance=±5% resistance=1k package=THT]
  LM358 = LM358 [package=dip08]
  5in = Header 1 [package=1x01_offset]
  AIN/DIN = Header 2 [package=screwterminal-3.5mm-2_lock]
  24in = Header 1 [package=1x01_offset]
  3V3in = Header 1 [package=1x01_offset]
  AIN = Header 1 [package=1x01_offset]
  PWR/GND = Header 2 [package=screwterminal-3.5mm-2_lock]
  Part1 = Adafruit Feather HUZZAH ESP8266 [part_number="Adafruit #2821"]

nets:
  N1: R6.Pin_0, R5.Pin_1
  N2: R6.Pin_1, R7.Pin_0, D2.anode
  N3: R9.Pin_0, R8.Pin_1
  N4: R9.Pin_1, R10.Pin_0, LM358.G$1_+IN
  N5: R2.Pin_0, R1.Pin_1
  N6: R2.Pin_1, D1.anode, R3.Pin_0
  N7: R8.Pin_0, D2.cathode, 3V3in.1
  N8: R5.Pin_0, D1.cathode, 5in.1
  N9: R1.Pin_0, 24in.1
  GND: R7.Pin_1, R10.Pin_1, R4.Pin_1, R13.Pin_1, LM358.G$1_V-, PWR/GND.2, Part1.GND
  N10: R3.Pin_1, R4.Pin_0
  N11: R12.Pin_0, R11.Pin_1
  N12: R12.Pin_1, R13.Pin_0, LM358.G$1_V+
  3.3: R11.Pin_0, PWR/GND.1, Part1.3.3V
  N13: LM358.G$1_OUT, LM358.G$1_-IN, Part1.ADC
  N14: AIN/DIN.1, AIN.1
  DIN: AIN/DIN.2, Part1.GPIO2

custom parts:
  Adafruit Feather HUZZAH ESP8266: his is the Adafruit Feather HUZZAH ESP8266 - our take on an 'all-in-one' ESP8266 WiFi development board with built in USB and battery charging. Its an ESP8266 WiFi module with all the extras you need, ready to rock! We have other boards in the Feather family, check'em out here. At the Feather HUZZAH's heart is an ESP8266 WiFi microcontroller clocked at 80 MHz and at 3.3V logic. This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

// code stored in the sketch: Untitled.ino

